// Logisim project Lab1.circ as structural Verilog: 7 circuits, main circuit main
module main (
);

  wire circuito_1_otherresets, clock_1_out;
  wire [2:0] BTNBUS;
  wire [6:0] circuito_1_columntodisplay;
  wire [9:0] KBDBUS;
  wire [34:0] LED0, LED6, LED11, LED16, LED21, LED26, LED31, LED36, LED41, LED46, LED51, LED56;

  Button ResetBtn (.out(BTNBUS[0]));
  Clock clock_1 (.out(clock_1_out));
  Button LoadMessage (.out(BTNBUS[1]));
  Keyboard #(.buflen(64)) keyboard_1 (
    .clk(clock_1_out), .re(KBDBUS[9]), .clr(KBDBUS[8]), .avail(KBDBUS[7]), .data(KBDBUS[6:0]));
  Button ShowMessage (.out(BTNBUS[2]));
  DotMatrix #(.matrixcols(60)) dotmatrix_1 (
    .col0(LED56[34:28]), .col1(LED56[27:21]), .col2(LED56[20:14]), .col3(LED56[13:7]), .col4(LED56[6:0]),
    .col5(LED51[34:28]), .col6(LED51[27:21]), .col7(LED51[20:14]), .col8(LED51[13:7]), .col9(LED51[6:0]),
    .col10(LED46[34:28]), .col11(LED46[27:21]), .col12(LED46[20:14]), .col13(LED46[13:7]),
    .col14(LED46[6:0]), .col15(LED41[34:28]), .col16(LED41[27:21]), .col17(LED41[20:14]),
    .col18(LED41[13:7]), .col19(LED41[6:0]), .col20(LED36[34:28]), .col21(LED36[27:21]),
    .col22(LED36[20:14]), .col23(LED36[13:7]), .col24(LED36[6:0]), .col25(LED31[34:28]),
    .col26(LED31[27:21]), .col27(LED31[20:14]), .col28(LED31[13:7]), .col29(LED31[6:0]),
    .col30(LED26[34:28]), .col31(LED26[27:21]), .col32(LED26[20:14]), .col33(LED26[13:7]),
    .col34(LED26[6:0]), .col35(LED21[34:28]), .col36(LED21[27:21]), .col37(LED21[20:14]),
    .col38(LED21[13:7]), .col39(LED21[6:0]), .col40(LED16[34:28]), .col41(LED16[27:21]),
    .col42(LED16[20:14]), .col43(LED16[13:7]), .col44(LED16[6:0]), .col45(LED11[34:28]),
    .col46(LED11[27:21]), .col47(LED11[20:14]), .col48(LED11[13:7]), .col49(LED11[6:0]), .col50(LED6[34:28]),
    .col51(LED6[27:21]), .col52(LED6[20:14]), .col53(LED6[13:7]), .col54(LED6[6:0]), .col55(LED0[34:28]),
    .col56(LED0[27:21]), .col57(LED0[20:14]), .col58(LED0[13:7]), .col59(LED0[6:0]));
  Circuito circuito_1 (
    .BTNBUS(BTNBUS), .KBDBUS(KBDBUS), .OTHERRESETS(circuito_1_otherresets),
    .COLUMNTODISPLAY(circuito_1_columntodisplay));
  pantalla pantalla_1 (
    .DIN(circuito_1_columntodisplay), .RESET(circuito_1_otherresets), .LED0(LED0), .LED6(LED6),
    .LED11(LED11), .LED16(LED16), .LED21(LED21), .LED26(LED26), .LED31(LED31), .LED36(LED36), .LED41(LED41),
    .LED46(LED46), .LED51(LED51), .LED56(LED56));
endmodule

module Circuito (
  input  [2:0] BTNBUS,
  input  [9:0] KBDBUS,
  output OTHERRESETS,
  output [6:0] COLUMNTODISPLAY
);

  wire and_2_out, and_3_out, and_4_out, clock_1_out, comparator_1_eq, comparator_2_eq, ENDOFLETTERS,
       not_1_out, not_3_out, NOTAVAILABLE, or_2_out, or_3_out, RAMCLK, RESETRAMADR, RESETROMCOUNTER,
       ROMCOUNTERFULLCYCLE, SHOWMESSAGE, WRITINGCLOCK_out;
  wire [2:0] contadora5_1_count;
  wire [6:0] CURRENTRAMADR, MSGLENGTH, register_1_q;
  wire [19:0] RAMOUTPUT, romaddress_1_out_3;

  not not_1 (not_1_out, KBDBUS[9]);
  not not_2 (NOTAVAILABLE, KBDBUS[7]);
  or or_1 (RESETRAMADR, BTNBUS[0], ENDOFLETTERS, BTNBUS[2]);
  Comparator #(.width(7)) comparator_1 (.a(CURRENTRAMADR), .b(MSGLENGTH), .eq(comparator_1_eq));  // open: gt, lt
  or or_2 (or_2_out, RESETRAMADR, not_1_out);
  and and_1 (ENDOFLETTERS, ROMCOUNTERFULLCYCLE, comparator_1_eq);
  Clock clock_1 (.out(clock_1_out));
  and and_2 (and_2_out, NOTAVAILABLE, SHOWMESSAGE);
  or or_3 (or_3_out, KBDBUS[7], RESETROMCOUNTER);
  and and_3 (and_3_out, NOTAVAILABLE, clock_1_out);
  RamAddress ramaddress_1 (.RESET(or_2_out), .CLK(RAMCLK), .out_3(CURRENTRAMADR));
  and and_4 (and_4_out, KBDBUS[7], KBDBUS[9]);
  D_Flip_Flop d_ff_1 (.D(1'b1), .clk(BTNBUS[1]), .Q(KBDBUS[9]), .reset(BTNBUS[0]));  // open: Qn, preset
  RAM #(.addrWidth(7), .clearpin("true"), .dataWidth(20)) ram_1 (
    .addr(CURRENTRAMADR), .we(and_4_out), .oe(NOTAVAILABLE), .clk(RAMCLK), .din({{13{1'b0}}, KBDBUS[6:0]}),
    .dout(RAMOUTPUT), .clr(BTNBUS[0]));
  ContadorA5 contadora5_1 (.CLK(and_3_out), .X(and_2_out), .RESET(or_3_out), .COUNT(contadora5_1_count));
  Comparator #(.width(3)) comparator_2 (.a(contadora5_1_count), .b(3'b101), .eq(comparator_2_eq));  // open: gt, lt
  or or_4 (RESETROMCOUNTER, BTNBUS[0], BTNBUS[1], BTNBUS[2]);
  D_Flip_Flop d_ff_2 (
    .D(comparator_2_eq), .clk(and_3_out), .Q(ROMCOUNTERFULLCYCLE), .reset(BTNBUS[0]));  // open: Qn, preset
  ROM #(.addrWidth(20), .dataWidth(7)) rom_1 (.addr(romaddress_1_out_3), .data(COLUMNTODISPLAY));
  RomAddress romaddress_1 (.DIN(RAMOUTPUT), .COUNT(contadora5_1_count), .out_3(romaddress_1_out_3));
  Clock WRITINGCLOCK (.out(WRITINGCLOCK_out));
  D_Flip_Flop d_ff_3 (.D(1'b1), .clk(BTNBUS[2]), .Q(SHOWMESSAGE), .reset(BTNBUS[0]));  // open: Qn, preset
  Register #(.width(7)) register_1 (.D(CURRENTRAMADR), .en(not_3_out), .clk(RAMCLK), .Q(register_1_q), .clr(BTNBUS[0]));
  not not_3 (not_3_out, SHOWMESSAGE);
  Multiplexer multiplexer_1 (.in0(ROMCOUNTERFULLCYCLE), .in1(WRITINGCLOCK_out), .out(RAMCLK), .sel(KBDBUS[7]));
  Adder #(.width(7)) adder_1 (.a(register_1_q), .b(7'b0000001), .out(MSGLENGTH));  // open: cin, cout

  assign KBDBUS[8] = BTNBUS[0];
  assign OTHERRESETS = BTNBUS[0];

  // Other names for the same wires on the sheet: KDBDATA[6:0] = KBDBUS[6:0]; RESETBTNSIGNAL = BTNBUS[0];
  //   RESETKBD = BTNBUS[0]; RESETRAMVALUES = BTNBUS[0]; LOADMESSAGEBTNSIGNAL = BTNBUS[1];
  //   SHOWMESSAGEBTNSIGNAL = BTNBUS[2]; AVAILABLE = KBDBUS[7]; KBDENABLE = KBDBUS[9]

  // Notes on the sheet:
  //   Señales del teclado
  //   * Limpiar Teclado
  //   * Limpiar Ram
  //   * Limpiar Flip Flops
  //   * Limpiar Pantalla
  //   Comportamiento de la ram
  //   Comportamiento de la rom
  //   Funcionamiento cuando hacemos click al Reset
  //   Comportamiento del reset de la direccion de la ram
  //   Señales de los botones
  //   Funcionamiento cuando iniciamos el cargado del mensaje en la RAM
  //   Comportamiento para resetear el contador de la rom
  //   contents of rom_1 (hex, n*v repeats v):
  //   8*0 7d 4*0 60 0 60 0 0 14 7f 14 7f 14 0 12 2a 7f 2a 24 0 1 26 8 32 40 0 2c 52 5a 24 a 0 0 0 60 4*0
  //   3e 41 5*0 41 3e 0 0 28 10 7c 10 28 0 8 8 3e 8 8 0 0 1 2 4*0 8 8 8 4*0 2 0 0 0 1 6 8 30 40 0 3e 45 49
  //   51 3e 0 11 21 7f 1 1 0 31 43 45 49 31 0 41 49 49 49 36 0 c 14 24 7f 4 0 79 49 49 49 46 0 1e 29 49 49
  //   46 0 61 42 44 48 70 0 36 49 49 49 36 0 31 49 49 4a 3c 0 0 0 22 4*0 1 22 0 0 0 8 14 22 41 0 0 5*14 0
  //   0 41 22 14 8 0 20 40 45 48 30 0 3e 41 5d 4d 38 0 3f 48 48 48 3f 0 7f 49 49 49 36 0 3e 41 41 41 22 0
  //   7f 41 41 22 1c 0 7f 49 49 49 41 0 7f 48 48 40 40 0 3e 41 49 49 4e 0 7f 8 8 8 7f 0 41 41 7f 41 41 0
  //   46 41 41 7e 40 0 7f 8 18 24 43 0 7f 4*1 0 7f 20 10 20 7f 0 7f 20 18 6 7f 0 3e 41 41 41 3e 0 7f 48 48
  //   48 30 0 3e 41 4d 42 3d 0 7f 48 4c 4a 31 0 31 49 49 49 46 0 40 40 7f 40 40 0 7e 1 1 1 7e 0 70 c 3 c
  //   70 0 7e 1 e 1 7e 0 63 14 8 14 63 0 70 8 7 8 70 0 43 45 49 51 61 0 0 0 7f 41 0 0 40 30 8 6 1 0 0 41
  //   7f 0 0 0 10 20 40 20 10 0 5*1 0 0 40 20 0 0 0 4 2a 2a 2a 1c 0 0 7f 9 9 6 0 0 1c 22 22 22 0 0 6 9 9
  //   7f 0 1c 2a 2a 2a 18 0 0 3f 48 48 20 0 0 32 49 49 3e 0 0 3f 4 4 7 5*0 2f 0 0 0 1 1 5e 0 0 7f 8 14 23
  //   0 0 0 3e 1 1 0 f 10 f 10 f 0 1f 8 10 10 f 0 e 11 11 11 e 0 0 1f 24 24 18 0 0 18 24 24 1f 0 0 f 8 8 8
  //   0 0 9 15 15 12 0 0 10 7e 11 11 0 1e 1 1 1 1e 0 1c 2 1 2 1c 0 1e 1 6 1 1e 0 11 a 4 a 11 0 10 8 7 8 10
  //   0 11 13 15 19 11 0 0 0 2a 55 41 5*0 7f 0 0 0 41 5d 2a 0 8 10 8 4 8 0 8 1c 2a 8 8
  //   Controlador de reloj de la ram
  //   Conteo de Caracteres introducidos
  //   El reloj de lectura corresponde al flanco de subida generado
  //   por completar un ciclo en el contador de la rom
  //   Funcionamiento cuando iniciamos a mostrar el mensaje en la pantalla
endmodule

module ContadorA5 (
  input  CLK,
  input  X,
  input  RESET,
  output [2:0] COUNT
);

  wire and_1_out, and_2_out, and_3_out, and_4_out, and_5_out, NotQ0, NotQ1, NotQ2, or_1_out;

  and and_1 (and_1_out, X, NotQ1);
  or or_1 (or_1_out, and_1_out, and_2_out);
  and and_2 (and_2_out, X, NotQ2);
  and and_3 (and_3_out, COUNT[0], X, NotQ2);
  and and_4 (and_4_out, X, COUNT[0], COUNT[1], NotQ2);
  and and_5 (and_5_out, X, COUNT[0], NotQ1);
  J_K_Flip_Flop j_k_ff_1 (
    .J(or_1_out), .K(or_1_out), .clk(CLK), .Q(COUNT[0]), .Qn(NotQ0), .reset(RESET));  // open: preset
  J_K_Flip_Flop j_k_ff_2 (
    .J(and_3_out), .K(and_3_out), .clk(CLK), .Q(COUNT[1]), .Qn(NotQ1), .reset(RESET));  // open: preset
  J_K_Flip_Flop j_k_ff_3 (
    .J(and_4_out), .K(and_5_out), .clk(CLK), .Q(COUNT[2]), .Qn(NotQ2), .reset(RESET));  // open: preset

  // Other names for the same wires on the sheet: Q0 = COUNT[0]; Q1 = COUNT[1]; Q2 = COUNT[2]

  // Notes on the sheet:
  //   SALIDA Q2
  //   SALIDA Q0
  //   SALIDA Q1
endmodule

module ten_registers (
  input  [6:0] DIN,
  input  CLK,
  input  RESET,
  output [6:0] DO1,
  output [6:0] DO2,
  output [6:0] DO3,
  output [6:0] DO4,
  output [6:0] DO5,
  output [6:0] DO6,
  output [6:0] DO7,
  output [6:0] DO8,
  output [6:0] DO9,
  output [6:0] DO10
);

  Register #(.width(7)) register_1 (.D(DIN), .clk(CLK), .Q(DO1), .clr(RESET));  // open: en
  Register #(.width(7)) register_2 (.D(DO1), .clk(CLK), .Q(DO2), .clr(RESET));  // open: en
  Register #(.width(7)) register_3 (.D(DO2), .clk(CLK), .Q(DO3), .clr(RESET));  // open: en
  Register #(.width(7)) register_4 (.D(DO3), .clk(CLK), .Q(DO4), .clr(RESET));  // open: en
  Register #(.width(7)) register_5 (.D(DO4), .clk(CLK), .Q(DO5), .clr(RESET));  // open: en
  Register #(.width(7)) register_6 (.D(DO5), .clk(CLK), .Q(DO6), .clr(RESET));  // open: en
  Register #(.width(7)) register_7 (.D(DO6), .clk(CLK), .Q(DO7), .clr(RESET));  // open: en
  Register #(.width(7)) register_8 (.D(DO7), .clk(CLK), .Q(DO8), .clr(RESET));  // open: en
  Register #(.width(7)) register_9 (.D(DO8), .clk(CLK), .Q(DO9), .clr(RESET));  // open: en
  Register #(.width(7)) register_10 (.D(DO9), .clk(CLK), .Q(DO10), .clr(RESET));  // open: en
endmodule

module pantalla (
  input  [6:0] DIN,
  input  RESET,
  output [34:0] LED0,
  output [34:0] LED6,
  output [34:0] LED11,
  output [34:0] LED16,
  output [34:0] LED21,
  output [34:0] LED26,
  output [34:0] LED31,
  output [34:0] LED36,
  output [34:0] LED41,
  output [34:0] LED46,
  output [34:0] LED51,
  output [34:0] LED56
);

  wire CLK;

  Clock clock_1 (.out(CLK));
  ten_registers ten_registers_1 (
    .DIN(DIN), .CLK(CLK), .RESET(RESET), .DO1(LED0[6:0]), .DO2(LED0[13:7]), .DO3(LED0[20:14]),
    .DO4(LED0[27:21]), .DO5(LED0[34:28]), .DO6(LED6[6:0]), .DO7(LED6[13:7]), .DO8(LED6[20:14]),
    .DO9(LED6[27:21]), .DO10(LED6[34:28]));
  ten_registers ten_registers_2 (
    .DIN(LED6[34:28]), .CLK(CLK), .RESET(RESET), .DO1(LED11[6:0]), .DO2(LED11[13:7]), .DO3(LED11[20:14]),
    .DO4(LED11[27:21]), .DO5(LED11[34:28]), .DO6(LED16[6:0]), .DO7(LED16[13:7]), .DO8(LED16[20:14]),
    .DO9(LED16[27:21]), .DO10(LED16[34:28]));
  ten_registers ten_registers_3 (
    .DIN(LED16[34:28]), .CLK(CLK), .RESET(RESET), .DO1(LED21[6:0]), .DO2(LED21[13:7]), .DO3(LED21[20:14]),
    .DO4(LED21[27:21]), .DO5(LED21[34:28]), .DO6(LED26[6:0]), .DO7(LED26[13:7]), .DO8(LED26[20:14]),
    .DO9(LED26[27:21]), .DO10(LED26[34:28]));
  ten_registers ten_registers_4 (
    .DIN(LED26[34:28]), .CLK(CLK), .RESET(RESET), .DO1(LED31[6:0]), .DO2(LED31[13:7]), .DO3(LED31[20:14]),
    .DO4(LED31[27:21]), .DO5(LED31[34:28]), .DO6(LED36[6:0]), .DO7(LED36[13:7]), .DO8(LED36[20:14]),
    .DO9(LED36[27:21]), .DO10(LED36[34:28]));
  ten_registers ten_registers_5 (
    .DIN(LED36[34:28]), .CLK(CLK), .RESET(RESET), .DO1(LED41[6:0]), .DO2(LED41[13:7]), .DO3(LED41[20:14]),
    .DO4(LED41[27:21]), .DO5(LED41[34:28]), .DO6(LED46[6:0]), .DO7(LED46[13:7]), .DO8(LED46[20:14]),
    .DO9(LED46[27:21]), .DO10(LED46[34:28]));
  ten_registers ten_registers_6 (
    .DIN(LED46[34:28]), .CLK(CLK), .RESET(RESET), .DO1(LED51[6:0]), .DO2(LED51[13:7]), .DO3(LED51[20:14]),
    .DO4(LED51[27:21]), .DO5(LED51[34:28]), .DO6(LED56[6:0]), .DO7(LED56[13:7]), .DO8(LED56[20:14]),
    .DO9(LED56[27:21]), .DO10(LED56[34:28]));
endmodule

module RamAddress (
  input  RESET,
  input  CLK,
  output [6:0] out_3
);

  Counter #(.max('h7f), .width(7)) counter_1 (.clr(RESET), .clk(CLK), .Q(out_3));  // open: load, up, count, D, carry
endmodule

module RomAddress (
  input  [19:0] DIN,
  input  [2:0] COUNT,
  output [19:0] out_3
);

  wire comparator_1_eq;
  wire [19:0] multiplexer_1_out, multiplier_1_out, subtractor_1_out;

  Comparator #(.width(20)) comparator_1 (.a(DIN), .b({20{1'b0}}), .eq(comparator_1_eq));  // open: gt, lt
  Multiplexer #(.width(20)) multiplexer_1 (.in0(DIN), .in1(20'h20), .out(multiplexer_1_out), .sel(comparator_1_eq));
  Subtractor #(.width(20)) subtractor_1 (.a(multiplexer_1_out), .b(20'h20), .out(subtractor_1_out));  // open: bin, bout
  Multiplier #(.width(20)) multiplier_1 (.a(subtractor_1_out), .b(20'h6), .out(multiplier_1_out));  // open: cin, cout
  Adder #(.width(20)) adder_1 (.a(multiplier_1_out), .b({{17{1'b0}}, COUNT}), .out(out_3));  // open: cin, cout
endmodule
